# Fritzing sketch RF-ROVER-2017-v1.1 (saved by Fritzing 0.9.3b)
circuit board: 8cm x 9cm
breadboards: 1

parts:
  SR1 = 74HC595 [package="DIP16 [THT]"]
  HB2 = H-Bridge [package=THT]
  VCC-LOAD1 = Battery block 9V
  R2 = Resistor [tolerance=±5% resistance=220 package=THT]
  R1 = Resistor [tolerance=±5% resistance=220 package=THT]
  ARDUINO_NANO1 = Arduino Nano (Rev3.0)
  LOAD1 = molex pin header, 4 pins [form=molex]
  LOAD2 = molex pin header, 4 pins [form=molex]
  HB1 = H-Bridge [package=THT]
  RF1 = RF24 BREAKOUT HEADER [form="♀ (female)" package=THT]
  C2 = Ceramic Capacitor [capacitance=100nF package="200 mil [THT, multilayer]"]
  C1 = Ceramic Capacitor [capacitance=100nF package="200 mil [THT, multilayer]"]
  VCC-LOGIC1 = Battery block 9V

nets:
  N1: SR1.Q1, HB2.4A
  N2: SR1.Q2, HB2.1A
  N3: SR1.Q3, HB2.2A
  N4: SR1.Q4, HB1.1A
  N5: SR1.Q5, HB1.2A
  N6: SR1.Q6, HB1.3A
  N7: SR1.Q7, HB1.4A
  GND: SR1.GND, SR1.OE, HB2.GND1, HB2.GND2, HB2.GND3, HB2.GND4, VCC-LOAD1.-, ARDUINO_NANO1.GND, HB1.GND1, HB1.GND2, HB1.GND3, HB1.GND4, RF1.GND, C2.1, C1.1, VCC-LOGIC1.-
  VCC: SR1.MR, SR1.VCC, HB2.VCC1, ARDUINO_NANO1.5V, HB1.VCC1, VCC-LOGIC1.+
  N8: SR1.SH_CP, ARDUINO_NANO1.D4
  N9: SR1.ST_CP, ARDUINO_NANO1.D3
  N10: SR1.DS, ARDUINO_NANO1.D2
  N11: SR1.Q0, HB2.3A
  N12: HB2.1_2EN, HB2.3_4EN, R2.Pin_0, C2.0
  N13: HB2.1Y, LOAD2.pin2
  N14: HB2.2Y, LOAD2.pin1
  N15: HB2.VCC2, VCC-LOAD1.+, HB1.VCC2
  N16: HB2.3Y, LOAD1.pin4, LOAD2.pin4, HB1.1Y
  N17: HB2.4Y, LOAD1.pin3, LOAD2.pin3, HB1.2Y
  N18: R2.Pin_1, ARDUINO_NANO1.D5
  N19: R1.Pin_0, HB1.1_2EN, HB1.3_4EN, C1.0
  N20: R1.Pin_1, ARDUINO_NANO1.D6
  N21: ARDUINO_NANO1.D9, RF1.CE
  N22: ARDUINO_NANO1.D10, RF1.CSN
  N23: ARDUINO_NANO1.D11/MOSI, RF1.MOSI
  N24: ARDUINO_NANO1.D12/MISO, RF1.MISO
  3V3: ARDUINO_NANO1.3V3, RF1.VCC
  N25: ARDUINO_NANO1.D13/SCK, RF1.SCK
  N26: LOAD1.pin1, HB1.4Y
  N27: LOAD1.pin2, HB1.3Y

notes:
  Designed by:
  MERIDIUM TECHNOLOGIES
  Upper Rail = VCC Logic (5V)
  HIGH VOLTAGE FOR MOTORS
  RF24 => 3.3V
  Motors 1-2
  Motors 3-4
