# Fritzing sketch RF24-RC-v02 (saved by Fritzing 0.9.3b)
circuit board: 4cm x 6cm
breadboards: 1

parts:
  RF1 = RF24 BREAKOUT HEADER [form="♀ (female)" package=THT]
  ARDUINO_NANO = Arduino Nano (Rev3.0)
  JOY = female pin header, 6 pins [form="♀ (female)"]

nets:
  GND: RF1.GND, ARDUINO_NANO.GND, JOY.pin4, JOY.pin5
  N1: RF1.CE, ARDUINO_NANO.D9
  N2: RF1.SCK, ARDUINO_NANO.D13/SCK
  N3: RF1.MISO, ARDUINO_NANO.D12/MISO
  N4: RF1.MOSI, ARDUINO_NANO.D11/MOSI
  N5: RF1.CSN, ARDUINO_NANO.D10
  VCC: RF1.VCC, ARDUINO_NANO.3V3
  N6: ARDUINO_NANO.VIN, JOY.pin6
  N7: ARDUINO_NANO.5V, JOY.pin3
  N8: ARDUINO_NANO.A7, JOY.pin2
  N9: ARDUINO_NANO.A6, JOY.pin1

notes:
  RF24
  A6
  A7
  5V
  GND
  9V
  ARDUINO NANO
  ------->
  MERIDIUM TECHNOLOGIES
